// Digital circuit control.dig as structural Verilog
module control (
  input  CLK,
  input  run,
  input  Z,
  input  C,
  input  [4:0] OPC,
  input  auto,
  output [1:0] cycle_o,
  output [16:0] control_o,
  output HLT,
  output PC_inc,
  output PC_r,
  output PC_w,
  output RAM_r,
  output RAM_w,
  output IRH_w,
  output IRL_w,
  output IMM_sel,
  output DIR_sel,
  output IND_sel,
  output Rs_src,
  output Rd_w,
  output Rs_r,
  output SPC_r,
  output SPC_w,
  output ALU_r
);

  wire not_1_out;

  not not_1 (not_1_out, CLK);
  Counter #(.Bits(2)) Cycle (.en(run), .C(not_1_out), .clr(1'b0), .out(cycle_o));  // open: ovf
  ROM #(.AddrBits(9), .Bits(17)) Control (.A({OPC, Z, C, cycle_o}), .sel(1'b1), .D(control_o));
  assign {HLT, PC_inc, PC_r, PC_w, RAM_r, RAM_w, IRH_w, IRL_w, IMM_sel, DIR_sel, IND_sel, Rs_src, Rd_w, Rs_r, SPC_r, SPC_w, ALU_r} = auto ? control_o : 17'bz;  // Driver driver_1

  // Notes on the sheet:
  //   auto: Set to 1 to use the program controller.
  //   0 is manual
  //   contents of Control (hex, n*v repeats v):
  //   d400,d200,10000,0,d400,d200,10000,0,d400,d200,10000,0,d400,d200,10000,0,d400,d200,
  //   110,0,d400,d200,110,0,d400,d200,110,0,d400,d200,110,0,d400,d200,1090,0,d400,d200,
  //   1090,0,d400,d200,1090,0,d400,d200,1090,0,d400,d200,1050,0,d400,d200,1050,0,d400,d200,
  //   1050,0,d400,d200,1050,0,d400,d200,888,0,d400,d200,888,0,d400,d200,888,0,d400,d200,
  //   888,0,d400,d200,848,0,d400,d200,848,0,d400,d200,848,0,d400,d200,848,0,d400,d200,18,
  //   0,d400,d200,18,0,d400,d200,18,0,d400,d200,18,0,d400,d200,2080,0,d400,d200,2080,0,
  //   d400,d200,2080,0,d400,d200,2080,0,d400,d200,0,0,d400,d200,2080,0,d400,d200,0,0,d400,
  //   d200,2080,0,d400,d200,2080,0,d400,d200,0,0,d400,d200,2080,0,d400,d200,0,0,d400,d200,
  //   0,0,d400,d200,0,0,d400,d200,2080,0,d400,d200,2080,0,d400,d200,2080,0,d400,d200,2080,
  //   0,d400,d200,0,0,d400,d200,0,0,d400,d200,0,0,d400,d200,0,0,d400,d200,0,0,d400,d200,
  //   0,0,d400,d200,0,0,d400,d200,0,0,d400,d200,0,0,d400,d200,0,0,d400,d200,0,0,d400,d200,
  //   0,0,d400,d200,0,0,d400,d200,0,0,d400,d200,0,0,d400,d200,0,0,d400,d200,0,0,d400,d200,
  //   0,0,d400,d200,11,0,d400,d200,11,0,d400,d200,11,0,d400,d200,11,0,d400,d200,11,0,d400,
  //   d200,11,0,d400,d200,11,0,d400,d200,11,0,d400,d200,11,0,d400,d200,11,0,d400,d200,11,
  //   0,d400,d200,11,0,d400,d200,11,0,d400,d200,11,0,d400,d200,11,0,d400,d200,11,0,d400,
  //   d200,11,0,d400,d200,11,0,d400,d200,11,0,d400,d200,11,0,d400,d200,11,0,d400,d200,11,
  //   0,d400,d200,11,0,d400,d200,11,0,d400,d200,11,0,d400,d200,11,0,d400,d200,11,0,d400,
  //   d200,11,0,d400,d200,11,0,d400,d200,11,0,d400,d200,11,0,d400,d200,11,0,d400,d200,11,
  //   0,d400,d200,11,0,d400,d200,11,0,d400,d200,11,0,d400,d200,11,0,d400,d200,11,0,d400,
  //   d200,11,0,d400,d200,11,0,d400,d200,0,0,d400,d200,0,0,d400,d200,0,0,d400,d200,0,0,
  //   d400,d200,0,0,d400,d200,0,0,d400,d200,0,0,d400,d200,0,0,d400,d200,0,0,d400,d200,0,
  //   0,d400,d200,0,0,d400,d200,0,0,d400,d200,0,0,d400,d200,0,0,d400,d200,0,0,d400,d200,
  //   0,0,d400,d200,0,0,d400,d200,0,0,d400,d200,0,0,d400,d200,0,0,d400,d200,0,0,d400,d200,
  //   0,0,d400,d200,0,0,d400,d200
endmodule
