// Digital circuit cpu.dig as structural Verilog
module cpu (
  input  Clock,
  input  PC_inc,
  input  PC_r,
  input  PC_w,
  input  IRH_w,
  input  IRL_w,
  input  DIR8_sel,
  input  IMM_sel,
  input  Rs_src,
  input  Rd_w,
  input  Rs_r,
  input  IND_sel,
  input  SPC_r,
  input  SPC_w,
  input  RAM_r,
  input  RAM_w,
  input  ALU_r,
  input  HLT,
  input  auto,
  input  run,
  input  DIR11_sel,
  input  C_ctrl,
  input  C_src,
  input  Clock_2,
  input  manual,
  input  [15:0] BRKPT,
  output [1:0] Cycle_out,
  output [19:0] control_out,
  output [4:0] Opcode,
  output [15:0] PC,
  output [7:0] out_30,
  output [7:0] out_31,
  output [7:0] out_32,
  output [7:0] out_33,
  output [7:0] out_34,
  output [7:0] out_35,
  output [7:0] out_36,
  output [7:0] out_37
);

  wire alu_1_c_o, alu_1_z_o, ALU_r_t, C_ctrl_t, C_src_t, CLK, comparator_1_eq, DIR8_sel_t, DIR11_sel_t,
       HLT_t, IMM_sel_t, IND_sel_t, instruction_1_p11, instruction_1_p12, instruction_1_p13,
       instruction_1_p14, IRH_w_t, IRL_w_t, multiplexer_1_out, or_1_out, PC_inc_t, PC_r_t, PC_w_t, RAM_r_t,
       RAM_w_t, Rd_w_t, Rs_r_t, Rs_src_t, run_t, SPC_r_t, SPC_w_t, status_1_c_o, status_1_z_o;
  wire [7:0] ramsingleport_1_d, registers_1_p16, registers_1_p17;
  wire [15:0] pc_1_a_out;

  assign {C_src_t, C_ctrl_t, ALU_r_t, SPC_w_t, SPC_r_t, Rs_r_t, Rd_w_t, Rs_src_t, IND_sel_t, DIR11_sel_t, DIR8_sel_t, IMM_sel_t, IRL_w_t, IRH_w_t, RAM_w_t, RAM_r_t, PC_w_t, PC_r_t, PC_inc_t, HLT_t} = ~auto ? {C_src, C_ctrl, ALU_r, SPC_w, SPC_r, Rs_r, Rd_w, Rs_src, IND_sel, DIR11_sel, DIR8_sel, IMM_sel, IRL_w, IRH_w, RAM_w, RAM_r, PC_w, PC_r, PC_inc, HLT} : 20'bz;  // DriverInvSel driverinvsel_1
  pc pc_1 (
    .PC_inc(PC_inc_t), .CLK(CLK), .PC_r(PC_r_t), .PC_w(PC_w_t), .A_in(pc_1_a_out), .run(run_t),
    .A_out(pc_1_a_out), .PC(PC));
  Comparator #(.Bits(16)) comparator_1 (.a(PC), .b(BRKPT), .eq(comparator_1_eq));  // open: gt, lt
  RAMSinglePort #(.AddrBits(16), .isProgramMemory("true"), .Bits(8)) ramsingleport_1 (
    .A(pc_1_a_out), .str(RAM_w_t), .C(CLK), .ld(RAM_r_t), .D(ramsingleport_1_d));
  Multiplexer multiplexer_1 (.sel(manual), .in_0(Clock), .in_1(Clock_2), .out(multiplexer_1_out));
  or or_1 (or_1_out, comparator_1_eq, HLT_t);
  Break #(.Cycles(10000)) BRK (.brk(or_1_out));
  and and_1 (CLK, multiplexer_1_out, ~HLT_t);  // And
  // instruction instruction_1: pin names not known; wires that end beside it: ramsingleport_1_d, CLK, IRH_w_t, IRL_w_t, DIR8_sel_t, DIR11_sel_t, IMM_sel_t, Rs_src_t, pc_1_a_out, ramsingleport_1_d, instruction_1_p11, instruction_1_p12, instruction_1_p13, instruction_1_p14, Opcode
  D_FF d_ff_1 (.D(run), .C(~CLK), .Q(run_t));  // open: nQ
  // registers registers_1: pin names not known; wires that end beside it: pc_1_a_out, ramsingleport_1_d, CLK, instruction_1_p11, Rd_w_t, instruction_1_p14, instruction_1_p12, Rs_r_t, instruction_1_p13, DIR8_sel_t, IND_sel_t, SPC_r_t, SPC_w_t, pc_1_a_out, ramsingleport_1_d, registers_1_p16, registers_1_p17, out_30, out_31, out_32, out_33, out_34, out_35, out_37, out_36
  alu alu_1 (
    .ALU_0(registers_1_p16), .ALU_1(registers_1_p17), .OPC(Opcode), .C_i(status_1_c_o), .ALU_r(ALU_r_t),
    .D_o(ramsingleport_1_d), .Z_o(alu_1_z_o), .C_o(alu_1_c_o));
  status status_1 (
    .Z_alu(alu_1_z_o), .C_alu(alu_1_c_o), .ZC_w(ALU_r_t), .CLK(CLK), .C_ctrl(C_ctrl_t), .C_src(C_src_t),
    .Z_o(status_1_z_o), .C_o(status_1_c_o));
  // control control_1: pin names not known; wires that end beside it: pc_1_a_out, CLK, run_t, status_1_z_o, status_1_c_o, Opcode, auto, Cycle_out, control_out, HLT_t, PC_inc_t, PC_r_t, PC_w_t, RAM_r_t, RAM_w_t, IRH_w_t, IRL_w_t, IMM_sel_t, DIR8_sel_t, DIR11_sel_t, IND_sel_t, Rs_src_t, Rd_w_t, Rs_r_t, SPC_r_t, SPC_w_t, ALU_r_t, C_ctrl_t, C_src_t

  // Notes on the sheet:
  //   Clock: Hz: 20
  //   Rd_w: Write to destination register
  //   Rs_r: Read from source register
  //   auto: Switch CPU control to auto (use controller)
  //   or control manually, default 1
endmodule
