// Digital circuit instruction.dig as structural Verilog
module instruction (
  input  [7:0] D_in,
  input  CLK,
  input  IRH_w,
  input  IRL_w,
  input  Rs_src,
  input  INH,
  output [2:0] R_d,
  output [2:0] R_S0,
  output [2:0] R_S1,
  output CMP,
  output [4:0] OPC,
  output [10:0] opr11,
  output [7:0] opr8
);

  Register #(.Bits(8)) IR_H (.D(D_in), .C(CLK), .en(IRH_w), .Q({OPC, opr11[10:8]}));
  Register #(.Bits(8)) IR_L (.D(D_in), .C(CLK), .en(IRL_w), .Q(opr8));
  and and_1 (CMP, INH, opr8[7]);
  Multiplexer #(.Bits(3)) multiplexer_1 (.sel(Rs_src), .in_0(opr11[10:8]), .in_1(opr8[6:4]), .out(R_S0));

  assign opr11[7:0] = opr8;
  assign R_d = opr11[10:8];
  assign R_S1 = opr8[2:0];

  // Notes on the sheet:
  //   D_in: Data bus input
  //   IRH_w: Write high byte of instruction register
  //   IRL_w: Write low byte of instruction register
  //   R_d: Destination register
  //   R_S0: First source register
  //   R_S1: Second source register.
  //   Used in ALU for instructions that have 2 source registers,
  //   e.g. like add
  //   CMP: Used to indicate whether the CMP flag is set
  //   Used for CMP, where we do a SUBC, but 
  //   1. we ignore the carry, so just doing a subtract
  //   2. we don't write the result back to the register
  //   OPC: Opcode output
  //   Rs_src: Source register R_S0 can either be the first or 
  //   second operand, and this bit chooses which one.
  //   0=1st operand (bits 0-2 of IR_H)
  //   1=2nd operand (bits 4-6 of IR_L)
  //   INH: Inherent addressing mode
  //   opr11: 11-bit operand
  //   opr8: 8-bit operand
endmodule
